# Fritzing sketch CNC_TFT_IR (saved by Fritzing 1.0.4)
stripboards: 1

parts:
  Arduino_CNC_Shield_V3_00_4 = Arduino_CNC_V3.00
  A11 = lcd color display 1.3in 240x240 7pin interface [package=THT]  # not connected
  U19 = TMP36 [package=to-92-kit]
  J26 = female pin header, 4 pins [form="♀ (female)"]
  J27 = female pin header, 4 pins [form="♀ (female)"]
  J28 = female pin header, 7 pins [form="♀ (female)"]
  J24 = female pin header, 3 pins [form="♀ (female)"]
  J22 = female pin header, 13 pins [form="♀ (female)"]

nets:
  N1: Arduino_CNC_Shield_V3_00_4.Z.STEP, Arduino_CNC_Shield_V3_00_4.A.DIR
  N2: U19.VCC, J24.pin1, J22.pin5
  N3: U19.VOUT, J26.pin4, J27.pin3, J28.pin6, J28.pin7, J24.pin2
  N4: U19.GND, J27.pin4, J24.pin3
  N5: J26.pin2, J27.pin1
  N6: J26.pin3, J27.pin2
  N7: J28.pin2, J22.pin3
  N8: J28.pin3, J22.pin7
  N9: J28.pin4, J22.pin1
  N10: J28.pin5, J22.pin8

notes:
  5
  9
  1
  15
  10

custom parts:
  Arduino_CNC_V3.00: Protoneer Arduino CNC Shield V3.00 If using Grbl V0.9: The “A” axis can not be used (yet). The “SCL” (Arduino A5) pin is now used for 'Probing' input. The “End Stops Z+ & Z-” (Arduino D11) and “SpnEn” (Arduino D12) have been switched!
  lcd color display 1.3in 240x240 7pin interface: 1.3 Inch Color 240 x 240 IPS TFT LCD Display Screen Module Board 7 Pin 4 Wire ST7789VW Drive IC SPI interface.
